// Logisim project temporizador.circ as structural Verilog: 1 circuit, main circuit main
module main (
  input  hlt,
  input  clk,
  input  gotot0,
  output t0,
  output t1,
  output t2,
  output t3,
  output t4,
  output t5,
  output t6,
  output t7
);

  wire d_ff_1_q, d_ff_2_q, not_1_out;
  wire [2:0] counter_1_q;

  not not_1 (not_1_out, hlt);
  Counter #(.width(3), .max('h7)) counter_1 (
    .Q(counter_1_q), .clk(clk), .clr(d_ff_2_q));  // open: load, D, count, carry
  D_Flip_Flop d_ff_1 (.clk(clk), .D(gotot0), .Q(d_ff_1_q));  // open: Qn, preset, en, reset
  Decoder #(.select(3), .disabled(0)) decoder_1 (
    .out0(t0), .out1(t1), .out2(t2), .out3(t3), .out4(t4), .out5(t5), .out6(t6), .out7(t7),
    .sel(counter_1_q), .en(not_1_out));
  D_Flip_Flop d_ff_2 (.clk(clk), .D(d_ff_1_q), .Q(d_ff_2_q));  // open: Qn, preset, en, reset
endmodule
