// Logisim project backup.circ as structural Verilog: 5 circuits, main circuit ULA v2
module ULA_v2 (
  input  [7:0] A,
  input  [2:0] Select,
  input  Clear,
  input  Clock,
  input  Enable,
  output Z,
  output N,
  output [7:0] Exit,
  output [7:0] Debug
);

  wire [7:0] adder_1_out, and_1_out, not_1_out, or_1_out, undriven, undriven_2, undriven_3;

  // Probe on A
  Adder adder_1 (.a(A), .b(Debug), .out(adder_1_out));  // open: cin, cout
  assign and_1_out = A & Debug;  // AND_Gate and_1, 8 bits wide
  assign or_1_out = A | Debug;  // OR_Gate or_1, 8 bits wide
  assign not_1_out = ~Debug;  // NOT_Gate not_1, 8 bits wide
  Multiplexer #(.select(3), .width(8)) multiplexer_1 (
    .in0(adder_1_out), .in1(and_1_out), .in2(or_1_out), .in3(not_1_out), .in4(A), .in5(undriven),
    .in6(undriven_2), .in7(undriven_3), .out(Exit), .sel(Select), .en(1'b1));
  Register register_1 (.D(Exit), .en(Enable), .Q(Debug), .clk(Clock), .clr(Clear));
  nor nor_1 (Z, Exit[0], Exit[1], Exit[2], Exit[3], Exit[4], Exit[5], Exit[6], Exit[7]);

  assign N = Exit[7];
endmodule

module ULA_v1 (
  input  [7:0] X,
  input  Clock,
  input  [7:0] Y,
  input  Enable,
  input  [2:0] Seletor,
  output [7:0] Carga,
  output [7:0] \Saída 
);

  wire [7:0] adder_1_out, and_1_out, not_1_out, not_2_out, not_3_out, or_1_out;

  Adder adder_1 (.a(X), .b(Y), .out(adder_1_out));  // open: cin, cout
  assign or_1_out = X | Y;  // OR_Gate or_1, 8 bits wide
  assign and_1_out = X & Y;  // AND_Gate and_1, 8 bits wide
  assign not_1_out = ~adder_1_out;  // NOT_Gate not_1, 8 bits wide
  assign not_2_out = ~and_1_out;  // NOT_Gate not_2, 8 bits wide
  assign not_3_out = ~and_1_out;  // NOT_Gate not_3, 8 bits wide
  Multiplexer #(.select(3), .width(8)) multiplexer_1 (
    .in0(adder_1_out), .in1(or_1_out), .in2(and_1_out), .in3(Y), .in4(not_1_out), .in5(not_2_out), .in6(X),
    .in7(not_3_out), .out(\Saída ), .sel(Seletor), .en(Enable));
  Register register_1 (.D(\Saída ), .Q(Carga), .clk(Clock));  // open: en, clr
  Register register_2 (.D(\Saída ), .Q(Carga), .clk(Clock));  // open: en, clr
endmodule

module Computador_V1 (
  input  On_Off,
  output [7:0] out_2,
  output Z,
  output N
);

  wire and_1_out, Clear, clock_1_out, clock_2_out, Clock_A, Clock_B, comparator_1_eq, comparator_1_gt,
       comparator_1_lt, comparator_2_eq, comparator_2_gt, not_1_out, or_1_out, or_2_out, or_3_out, s_r_ff_1_q;
  wire [7:0] A, B, counter_1_q, register_1_q, register_2_q, rom_1_data, subtractor_1_out, transistor_3_out,
       transistor_4_out;

  Counter counter_1 (.Q(counter_1_q), .clk(Clock_B), .clr(Clear));  // open: load, D, count, carry
  Transistor #(.\type ("n")) transistor_1 (.in(clock_2_out), .out(Clock_B), .gate(On_Off));
  Transistor #(.\type ("n")) transistor_2 (.in(clock_1_out), .out(Clock_A), .gate(On_Off));
  Clock clock_1 (.out(clock_1_out));
  Clock #(.highDuration(2), .lowDuration(2)) clock_2 (.out(clock_2_out));
  Button C (.out(Clear));
  ROM rom_1 (.addr(counter_1_q), .data(rom_1_data), .sel(1'b1));
  // Probe on out_2
  // Probe on A
  // Probe on B
  // Probe on transistor_3_out
  Transistor #(.\type ("n"), .width(8)) transistor_3 (.in(rom_1_data), .out(transistor_3_out), .gate(or_1_out));
  Transistor #(.\type ("n"), .width(8)) transistor_4 (.in(subtractor_1_out), .out(transistor_4_out), .gate(or_1_out));
  or or_1 (or_1_out, comparator_2_eq, comparator_2_gt);
  Subtractor subtractor_1 (.a(rom_1_data), .b(8'h1), .out(subtractor_1_out));  // open: bin, bout
  Register register_1 (.D(transistor_3_out), .en(comparator_1_gt), .Q(register_1_q), .clk(Clock_A), .clr(Clear));
  Comparator comparator_1 (
    .a(transistor_3_out), .b(8'h5), .gt(comparator_1_gt), .eq(comparator_1_eq), .lt(comparator_1_lt));
  or or_2 (or_2_out, comparator_1_eq, comparator_1_lt);
  or or_3 (or_3_out, comparator_1_gt, not_1_out);
  not not_1 (not_1_out, or_1_out);
  Comparator comparator_2 (
    .a(subtractor_1_out), .b({8{1'b0}}), .gt(comparator_2_gt), .eq(comparator_2_eq));  // open: lt
  and and_1 (and_1_out, or_2_out, or_1_out);
  Register register_2 (.D(transistor_4_out), .en(and_1_out), .Q(register_2_q), .clk(Clock_A), .clr(Clear));
  ROM rom_2 (.addr(register_1_q), .data(A), .sel(1'b1));
  S_R_Flip_Flop s_r_ff_1 (
    .S(and_1_out), .clk(Clock_A), .R(or_3_out), .Q(s_r_ff_1_q), .reset(Clear), .en(1'b1));  // open: Qn, preset
  ULA_v2 ula_v2_1 (
    .A(A), .Select(register_2_q[2:0]), .Exit(out_2), .Z(Z), .N(N), .Clock(Clock_B), .Clear(Clear),
    .Enable(s_r_ff_1_q), .Debug(B));

  // Notes on the sheet:
  //   Programa
  //   1 = add
  //   2 = and
  //   3 = or
  //   4 = not
  //   5 = bypass
  //   contents of rom_1 (hex, n*v repeats v):
  //   10 5 4 11 1 12
  //   Dados
  //   contents of rom_2 (hex, n*v repeats v):
  //   16*0 5 7
endmodule

module Memory_Block (
  input  Clock,
  input  Clear,
  input  [7:0] \Endereço ,
  input  Enable_REM,
  input  [7:0] \Saída ,
  input  Select,
  input  [7:0] Dados,
  input  Enable_RDM,
  input  Store,
  input  Load
);

  wire [7:0] multiplexer_1_out, ram_1_data, register_1_q;

  Register register_1 (.D(\Endereço ), .en(Enable_REM), .Q(register_1_q), .clk(Clock), .clr(Clear));
  RAM #(.bus("separate")) ram_1 (
    .addr(register_1_q), .din(\Saída ), .data(ram_1_data), .str(Store), .clk(Clock), .ld(Load), .clr(Clear));  // open: sel
  Multiplexer #(.width(8)) multiplexer_1 (
    .in0(ram_1_data), .in1(Dados), .out(multiplexer_1_out), .sel(Select), .en(1'b1));
  Register register_2 (.D(multiplexer_1_out), .en(Enable_RDM), .Q(\Saída ), .clk(Clock), .clr(Clear));
endmodule

module main (
  input  [7:0] in_1
);

  wire Clear, Clock;
  wire [7:0] ula_v2_1_debug, undriven, undriven_2;

  Clock clock_1 (.out(Clock));
  Button C (.out(Clear));
  // Probe on in_1
  Memory_Block memory_block_1 (
    .Clock(Clock), .Clear(Clear), .Dados(in_1), .\Saída (undriven_2), .\Endereço (undriven));  // open: Enable_REM, Store, Load, Select, Enable_RDM
  ULA_v2 ula_v2_1 (
    .A(undriven_2), .Exit(in_1), .Clock(Clock), .Clear(Clear), .Enable(1'b1), .Debug(ula_v2_1_debug));  // open: Select, Z, N
  // Probe on ula_v2_1_debug
  // Probe on in_1
endmodule
