// Logisim project main.circ as structural Verilog: 11 circuits, main circuit main
module ULA_v2 (
  input  [7:0] A,
  input  Carga_NZ,
  input  [2:0] Select,
  input  Clear,
  input  Clock,
  input  Enable,
  output Z,
  output N,
  output [7:0] Exit,
  output [7:0] AC_Exit
);

  wire nor_1_out;
  wire [7:0] adder_1_out, and_1_out, not_1_out, or_1_out, undriven, undriven_2, undriven_3;

  // Probe on A
  Adder adder_1 (.a(A), .b(AC_Exit), .out(adder_1_out));  // open: cin, cout
  assign and_1_out = A & AC_Exit;  // AND_Gate and_1, 8 bits wide
  assign or_1_out = A | AC_Exit;  // OR_Gate or_1, 8 bits wide
  assign not_1_out = ~AC_Exit;  // NOT_Gate not_1, 8 bits wide
  Multiplexer #(.select(3), .width(8)) multiplexer_1 (
    .in0(adder_1_out), .in1(and_1_out), .in2(or_1_out), .in3(not_1_out), .in4(A), .in5(undriven),
    .in6(undriven_2), .in7(undriven_3), .out(Exit), .sel(Select), .en(1'b1));
  Register register_1 (.D(Exit), .en(Enable), .Q(AC_Exit), .clk(Clock), .clr(Clear));
  Register #(.width(1)) register_2 (.D(nor_1_out), .en(Carga_NZ), .Q(Z), .clk(Clock), .clr(Clear));
  nor nor_1 (nor_1_out, Exit[0], Exit[1], Exit[2], Exit[3], Exit[4], Exit[5], Exit[6], Exit[7]);
  Register #(.width(1)) register_3 (.D(Exit[7]), .en(Carga_NZ), .Q(N), .clk(Clock), .clr(Clear));

  // Other names for the same wires on the sheet: clk = Clock; clr = Clear
endmodule

module ULA_v1 (
  input  [7:0] X,
  input  Clock,
  input  [7:0] Y,
  input  Enable,
  input  [2:0] Seletor,
  output [7:0] Carga,
  output [7:0] \Saída 
);

  wire [7:0] adder_1_out, and_1_out, not_1_out, not_2_out, not_3_out, or_1_out;

  Adder adder_1 (.a(X), .b(Y), .out(adder_1_out));  // open: cin, cout
  assign or_1_out = X | Y;  // OR_Gate or_1, 8 bits wide
  assign and_1_out = X & Y;  // AND_Gate and_1, 8 bits wide
  assign not_1_out = ~adder_1_out;  // NOT_Gate not_1, 8 bits wide
  assign not_2_out = ~and_1_out;  // NOT_Gate not_2, 8 bits wide
  assign not_3_out = ~and_1_out;  // NOT_Gate not_3, 8 bits wide
  Multiplexer #(.select(3), .width(8)) multiplexer_1 (
    .in0(adder_1_out), .in1(or_1_out), .in2(and_1_out), .in3(Y), .in4(not_1_out), .in5(not_2_out), .in6(X),
    .in7(not_3_out), .out(\Saída ), .sel(Seletor), .en(Enable));
  Register register_1 (.D(\Saída ), .Q(Carga), .clk(Clock));  // open: en, clr
  Register register_2 (.D(\Saída ), .Q(Carga), .clk(Clock));  // open: en, clr
endmodule

module Computador_V1 (
  input  On_Off,
  output [7:0] out_2,
  output Z,
  output N
);

  wire and_1_out, Clear, clock_1_out, clock_2_out, Clock_A, Clock_B, comparator_1_eq, comparator_1_gt,
       comparator_1_lt, comparator_2_eq, comparator_2_gt, not_1_out, or_1_out, or_2_out, or_3_out, s_r_ff_1_q;
  wire [7:0] A, B, counter_1_q, register_1_q, register_2_q, rom_1_data, subtractor_1_out, transistor_3_out,
       transistor_4_out;

  Counter counter_1 (.Q(counter_1_q), .clk(Clock_B), .clr(Clear));  // open: load, D, count, carry
  Transistor #(.\type ("n")) transistor_1 (.in(clock_2_out), .out(Clock_B), .gate(On_Off));
  Transistor #(.\type ("n")) transistor_2 (.in(clock_1_out), .out(Clock_A), .gate(On_Off));
  Clock clock_1 (.out(clock_1_out));
  Clock #(.highDuration(2), .lowDuration(2)) clock_2 (.out(clock_2_out));
  Button C (.out(Clear));
  ROM rom_1 (.addr(counter_1_q), .data(rom_1_data), .sel(1'b1));
  // Probe on out_2
  // Probe on A
  // Probe on B
  // Probe on transistor_3_out
  Transistor #(.\type ("n"), .width(8)) transistor_3 (.in(rom_1_data), .out(transistor_3_out), .gate(or_1_out));
  Transistor #(.\type ("n"), .width(8)) transistor_4 (.in(subtractor_1_out), .out(transistor_4_out), .gate(or_1_out));
  or or_1 (or_1_out, comparator_2_eq, comparator_2_gt);
  Subtractor subtractor_1 (.a(rom_1_data), .b(8'h1), .out(subtractor_1_out));  // open: bin, bout
  Register register_1 (.D(transistor_3_out), .en(comparator_1_gt), .Q(register_1_q), .clk(Clock_A), .clr(Clear));
  Comparator comparator_1 (
    .a(transistor_3_out), .b(8'h5), .gt(comparator_1_gt), .eq(comparator_1_eq), .lt(comparator_1_lt));
  or or_2 (or_2_out, comparator_1_eq, comparator_1_lt);
  or or_3 (or_3_out, comparator_1_gt, not_1_out);
  not not_1 (not_1_out, or_1_out);
  Comparator comparator_2 (
    .a(subtractor_1_out), .b({8{1'b0}}), .gt(comparator_2_gt), .eq(comparator_2_eq));  // open: lt
  and and_1 (and_1_out, or_2_out, or_1_out);
  Register register_2 (.D(transistor_4_out), .en(and_1_out), .Q(register_2_q), .clk(Clock_A), .clr(Clear));
  ROM rom_2 (.addr(register_1_q), .data(A), .sel(1'b1));
  S_R_Flip_Flop s_r_ff_1 (
    .S(and_1_out), .clk(Clock_A), .R(or_3_out), .Q(s_r_ff_1_q), .reset(Clear), .en(1'b1));  // open: Qn, preset
  // ULA_v2 ula_v2_1: pin names not known; wires that end beside it: Z, Clock_B, register_2_q[2:0], A, s_r_ff_1_q, Clock_B, N, out_2, B, Clear

  // Notes on the sheet:
  //   Programa
  //   1 = add
  //   2 = and
  //   3 = or
  //   4 = not
  //   5 = bypass
  //   contents of rom_1 (hex, n*v repeats v):
  //   10 5 4 11 1 12
  //   Dados
  //   contents of rom_2 (hex, n*v repeats v):
  //   16*0 5 7
endmodule

module Memory_Block (
  input  Clock,
  input  Clear,
  input  [7:0] \Endereço ,
  input  Enable_REM,
  input  Select,
  input  [7:0] Dados,
  input  Enable_RDM,
  input  Store,
  input  Load,
  output [7:0] \Saída 
);

  wire [7:0] multiplexer_1_out, ram_1_data, register_1_q;

  Register register_1 (.D(\Endereço ), .en(Enable_REM), .Q(register_1_q), .clk(Clock), .clr(Clear));
  RAM #(.bus("separate")) ram_1 (
    .addr(register_1_q), .din(\Saída ), .data(ram_1_data), .str(Store), .clk(Clock), .ld(Load));  // open: sel, clr
  Multiplexer #(.width(8)) multiplexer_1 (
    .in0(ram_1_data), .in1(Dados), .out(multiplexer_1_out), .sel(Select));  // open: en
  Register register_2 (.D(multiplexer_1_out), .en(Enable_RDM), .Q(\Saída ), .clk(Clock), .clr(Clear));
endmodule

module Instruction_Decoder (
  input  add,
  input  \and ,
  input  \or ,
  input  \not ,
  output [2:0] out_5
);

  or or_1 (out_5[0], \not , \and );
  or or_2 (out_5[1], \not , \or );
  nor nor_1 (out_5[2], add, \or , \and , \not );
  // Probe on out_5
endmodule

module Controller (
  input  clk,
  input  NOP,
  input  STA,
  input  LDA,
  input  ADD,
  input  OR,
  input  AND,
  input  NOT,
  input  JMP,
  input  JN,
  input  JZ,
  input  HLT,
  input  N,
  input  Z,
  input  rst,
  output gotot0,
  output cargaPC,
  output cargaNZ,
  output cargaAC,
  output ulaNot,
  output ulaAnd,
  output ulaOr,
  output ulaAdd,
  output ulaY,
  output write,
  output read,
  output cargaRDM,
  output sel,
  output cargaRI,
  output incrementaPC,
  output cargaREM
);

  wire and_1_out, and_2_out, and_3_out, and_4_out, and_5_out, and_6_out, and_7_out, and_8_out, and_9_out,
       and_10_out, and_11_out, and_12_out, and_14_out, and_15_out, and_22_out, and_23_out, and_26_out,
       and_27_out, and_28_out, not_1_out, not_2_out, or_1_out, or_2_out, or_3_out, or_4_out, or_5_out,
       or_6_out, or_7_out, or_8_out, or_9_out, or_10_out, timer_1_t0, timer_1_t1, timer_1_t3, timer_1_t4,
       timer_1_t5, timer_1_t6, timer_1_t7;

  not not_1 (not_1_out, N);
  not not_2 (not_2_out, Z);
  and and_1 (and_1_out, JN, not_1_out);
  and and_2 (and_2_out, JZ, not_2_out);
  and and_3 (and_3_out, JN, N);
  and and_4 (and_4_out, JZ, Z);
  and and_5 (and_5_out, JN, N);
  and and_6 (and_6_out, JZ, Z);
  and and_7 (and_7_out, JN, not_1_out);
  and and_8 (and_8_out, JZ, not_2_out);
  and and_9 (and_9_out, N, JN);
  and and_10 (and_10_out, Z, JZ);
  or or_1 (or_1_out, STA, LDA, ADD, OR, AND);
  or or_2 (or_2_out, NOP, NOT, and_1_out, and_2_out);
  or or_3 (or_3_out, JMP, and_3_out, and_4_out);
  or or_4 (or_4_out, LDA, ADD, OR, AND);
  or or_5 (or_5_out, STA, LDA, ADD, OR, AND, JMP, and_5_out, and_6_out);
  or or_6 (or_6_out, AND, OR, ADD, LDA);
  or or_7 (or_7_out, AND, OR, ADD, LDA, STA);
  or or_8 (or_8_out, and_7_out, and_8_out);
  or or_9 (or_9_out, STA, LDA, ADD, OR, AND, JMP, and_9_out, and_10_out);
  Timer timer_1 (
    .hlt(HLT), .clk(clk), .gotot0(or_10_out), .t0(timer_1_t0), .t1(timer_1_t1), .t2(cargaRI),
    .t3(timer_1_t3), .t4(timer_1_t4), .t5(timer_1_t5), .t6(timer_1_t6), .t7(timer_1_t7));
  or or_10 (or_10_out, gotot0, rst);
  and and_11 (and_11_out, timer_1_t7, or_1_out);
  and and_12 (and_12_out, timer_1_t3, or_2_out);
  and and_13 (cargaPC, timer_1_t5, or_3_out);
  and and_14 (and_14_out, timer_1_t7, or_4_out);
  and and_15 (and_15_out, timer_1_t3, NOT);
  and and_16 (ulaNot, timer_1_t3, NOT);
  and and_17 (ulaAnd, timer_1_t7, AND);
  and and_18 (ulaOr, timer_1_t7, OR);
  and and_19 (ulaAdd, timer_1_t7, ADD);
  and and_20 (ulaY, timer_1_t7, LDA);
  and and_21 (write, timer_1_t7, STA);
  and and_22 (and_22_out, timer_1_t4, or_5_out);
  and and_23 (and_23_out, timer_1_t6, or_6_out);
  and and_24 (cargaRDM, timer_1_t6, STA);
  and and_25 (sel, timer_1_t5, or_7_out);
  and and_26 (and_26_out, timer_1_t4, or_7_out);
  and and_27 (and_27_out, timer_1_t3, or_8_out);
  and and_28 (and_28_out, timer_1_t3, or_9_out);
  or or_11 (gotot0, and_11_out, and_12_out, cargaPC);
  or or_12 (cargaAC, and_14_out, and_15_out);
  or or_13 (read, timer_1_t1, and_22_out, and_23_out);
  or or_14 (incrementaPC, timer_1_t1, and_26_out, and_27_out);
  or or_15 (cargaREM, sel, and_28_out, timer_1_t0);

  assign cargaNZ = cargaAC;
endmodule

module Timer (
  input  hlt,
  input  clk,
  input  gotot0,
  output t0,
  output t1,
  output t2,
  output t3,
  output t4,
  output t5,
  output t6,
  output t7
);

  wire d_ff_1_q, d_ff_2_q, not_1_out;
  wire [2:0] counter_1_q;

  not not_1 (not_1_out, hlt);
  Counter #(.width(3), .max('h7)) counter_1 (
    .Q(counter_1_q), .clk(clk), .clr(d_ff_2_q));  // open: load, D, count, carry
  D_Flip_Flop d_ff_1 (.clk(clk), .D(gotot0), .Q(d_ff_1_q));  // open: Qn, preset, en, reset
  Decoder #(.select(3), .disabled(0)) decoder_1 (
    .out0(t0), .out1(t1), .out2(t2), .out3(t3), .out4(t4), .out5(t5), .out6(t6), .out7(t7),
    .sel(counter_1_q), .en(not_1_out));
  D_Flip_Flop d_ff_2 (.clk(clk), .D(d_ff_1_q), .Q(d_ff_2_q));  // open: Qn, preset, en, reset
endmodule

module main (
  input  [7:0] Dados,
  input  [7:0] \Memória 
);

  wire and_1_out, and_2_out, Apagar_out, button_1_out, clk, clock_2_out, controller_1_cargaac,
       controller_1_carganz, controller_1_cargapc, controller_1_cargardm, controller_1_cargarem,
       controller_1_cargari, controller_1_gotot0, controller_1_incrementapc, controller_1_read,
       controller_1_sel, controller_1_ulaadd, controller_1_ulaand, controller_1_ulanot, controller_1_ulaor,
       controller_1_write, decoder_1_out0, decoder_1_out1, decoder_1_out2, decoder_1_out3, decoder_1_out4,
       decoder_1_out5, decoder_1_out6, decoder_1_out7, decoder_1_out8, decoder_1_out9, decoder_1_out10,
       \Mudar_Posição_out , not_1_out, or_1_out, or_2_out, or_4_out, or_5_out, or_6_out, Salvar_out,
       transistor_1_out, transistor_2_out, ula_v2_1_n, ula_v2_1_z;
  wire [1:0] nand_1_out;
  wire [2:0] instruction_decoder_1_out_5;
  wire [3:0] \opcode_1_saída ;
  wire [7:0] counter_1_q, \memory_block_1_saída , multiplexer_1_out, multiplexer_2_out, multiplexer_3_out,
       register_1_q, ula_v2_1_exit;

  Clock clock_1 (.out(clk));
  Button button_1 (.out(button_1_out));
  Decoder #(.select(4)) decoder_1 (
    .out0(decoder_1_out0), .out1(decoder_1_out1), .out2(decoder_1_out2), .out3(decoder_1_out3),
    .out4(decoder_1_out4), .out5(decoder_1_out5), .out6(decoder_1_out6), .out7(decoder_1_out7),
    .out8(decoder_1_out8), .out9(decoder_1_out9), .out10(decoder_1_out10), .sel(\opcode_1_saída ));  // open: out11, out12, out13, out14, out15, en
  Controller controller_1 (
    .rst(button_1_out), .gotot0(controller_1_gotot0), .cargaPC(controller_1_cargapc),
    .cargaNZ(controller_1_carganz), .cargaAC(controller_1_cargaac), .ulaNot(controller_1_ulanot),
    .ulaAnd(controller_1_ulaand), .ulaOr(controller_1_ulaor), .ulaAdd(controller_1_ulaadd),
    .write(controller_1_write), .read(controller_1_read), .cargaRDM(controller_1_cargardm),
    .sel(controller_1_sel), .cargaRI(controller_1_cargari), .incrementaPC(controller_1_incrementapc),
    .cargaREM(controller_1_cargarem), .NOP(decoder_1_out10), .STA(decoder_1_out9), .LDA(decoder_1_out8),
    .ADD(decoder_1_out7), .OR(decoder_1_out6), .AND(decoder_1_out5), .NOT(decoder_1_out4),
    .JMP(decoder_1_out3), .JN(decoder_1_out2), .JZ(decoder_1_out1), .HLT(decoder_1_out0), .N(ula_v2_1_n),
    .Z(ula_v2_1_z), .clk(clk));  // open: ulaY
  OpCode opcode_1 (
    .CargaRI(controller_1_cargari), .Clock(clk), .Entrada(\memory_block_1_saída ), .\Saída (\opcode_1_saída ));  // open: Reset
  Counter counter_1 (
    .load(controller_1_cargapc), .D(\memory_block_1_saída ), .count(controller_1_incrementapc),
    .Q(counter_1_q), .clk(clk), .clr(or_1_out));  // open: carry
  not not_1 (not_1_out, controller_1_cargapc);
  or or_1 (or_1_out, button_1_out, controller_1_gotot0);
  Instruction_Decoder instruction_decoder_1 (
    .add(controller_1_ulaadd), .\and (controller_1_ulaand), .\or (controller_1_ulaor),
    .\not (controller_1_ulanot), .out_5(instruction_decoder_1_out_5));
  // Probe on Dados
  Button \Mudar_Posição  (.out(\Mudar_Posição_out ));
  Button Salvar (.out(Salvar_out));
  Button Apagar (.out(Apagar_out));
  nand nand_1 (nand_1_out[0], nand_1_out[1], not_1_out);
  ULA_v2 ula_v2_1 (
    .A(\memory_block_1_saída ), .Select(instruction_decoder_1_out_5), .Exit(ula_v2_1_exit), .Z(ula_v2_1_z),
    .N(ula_v2_1_n), .Clock(clk), .Enable(controller_1_cargaac), .Carga_NZ(controller_1_carganz));  // open: Clear, AC_Exit
  Multiplexer #(.width(8)) multiplexer_1 (
    .in0(Dados), .in1({8{1'b0}}), .out(multiplexer_1_out), .sel(Apagar_out));  // open: en
  // Probe on \Memória 
  Register register_1 (.D(\Memória ), .en(\Mudar_Posição_out ), .Q(register_1_q), .clk(clk));  // open: clr
  // Probe on multiplexer_2_out
  Multiplexer #(.select(2), .width(8)) multiplexer_2 (
    .in0(counter_1_q), .in1(\memory_block_1_saída ), .in2(register_1_q), .out(multiplexer_2_out),
    .sel(nand_1_out));  // open: in3, en
  or or_2 (or_2_out, controller_1_cargarem, nand_1_out[1]);
  Multiplexer #(.width(8)) multiplexer_3 (
    .in0(ula_v2_1_exit), .in1(multiplexer_1_out), .out(multiplexer_3_out), .sel(nand_1_out[1]));  // open: en
  // Probe on multiplexer_3_out
  Clock #(.highDuration(2), .lowDuration(2)) clock_2 (.out(clock_2_out));
  or or_3 (nand_1_out[1], Apagar_out, Salvar_out);
  or or_4 (or_4_out, controller_1_cargardm, nand_1_out[1]);
  or or_5 (or_5_out, and_2_out, controller_1_write);
  or or_6 (or_6_out, controller_1_sel, and_1_out);
  and and_1 (and_1_out, nand_1_out[1], transistor_2_out);
  Transistor #(.\type ("n")) transistor_1 (.in(clk), .out(transistor_1_out), .gate(nand_1_out[1]));
  Transistor #(.\type ("n")) transistor_2 (.in(clock_2_out), .out(transistor_2_out), .gate(nand_1_out[1]));
  // Probe on \memory_block_1_saída 
  Memory_Block memory_block_1 (
    .Clock(clk), .Enable_REM(or_2_out), .Dados(multiplexer_3_out), .\Endereço (multiplexer_2_out),
    .Store(or_5_out), .Load(controller_1_read), .Select(or_6_out), .Enable_RDM(or_4_out),
    .\Saída (\memory_block_1_saída ));  // open: Clear
  and and_2 (and_2_out, transistor_1_out, nand_1_out[1]);

  // Notes on the sheet:
  //   PC
endmodule

module OpCode (
  input  [7:0] Entrada,
  input  CargaRI,
  input  Reset,
  input  Clock,
  output [3:0] \Saída 
);

  Register #(.width(4)) register_1 (.D(Entrada[7:4]), .en(CargaRI), .Q(\Saída ), .clk(Clock), .clr(Reset));
endmodule

module mainAlt (
);

  wire clock_1_out, controller_1_cargaac, controller_1_carganz, controller_1_cargapc, controller_1_cargardm,
       controller_1_cargarem, controller_1_cargari, controller_1_incrementapc, controller_1_read,
       controller_1_sel, controller_1_ulaadd, controller_1_ulaand, controller_1_ulanot, controller_1_ulaor,
       controller_1_write, decoder_1_out0, decoder_1_out1, decoder_1_out2, decoder_1_out3, decoder_1_out4,
       decoder_1_out5, decoder_1_out6, decoder_1_out7, decoder_1_out8, decoder_1_out9, decoder_1_out10,
       ula_v2_1_n, ula_v2_1_z;
  wire [2:0] instruction_decoder_1_out_5;
  wire [3:0] \opcode_1_saída ;
  wire [7:0] counter_1_q, \memory_block_1_saída , multiplexer_1_out, register_1_q;

  Clock #(.highDuration(2), .lowDuration(2)) clock_1 (.out(clock_1_out));
  Register register_1 (.D(register_1_q), .en(controller_1_cargaac), .Q(register_1_q), .clk(clock_1_out));  // open: clr
  ULA_v2 ula_v2_1 (
    .A(register_1_q), .Select(instruction_decoder_1_out_5), .Exit(register_1_q), .Z(ula_v2_1_z),
    .N(ula_v2_1_n), .Clock(clock_1_out), .Carga_NZ(controller_1_carganz));  // open: Clear, Enable, AC_Exit
  Counter counter_1 (
    .load(controller_1_cargapc), .D(register_1_q), .count(controller_1_incrementapc), .Q(counter_1_q),
    .clk(clock_1_out));  // open: carry, clr
  Instruction_Decoder instruction_decoder_1 (
    .add(controller_1_ulaadd), .\and (controller_1_ulaand), .\or (controller_1_ulaor),
    .\not (controller_1_ulanot), .out_5(instruction_decoder_1_out_5));
  Multiplexer #(.width(8)) multiplexer_1 (
    .in0(counter_1_q), .in1(register_1_q), .out(multiplexer_1_out));  // open: sel, en
  Memory_Block memory_block_1 (
    .Clock(clock_1_out), .Enable_REM(controller_1_cargarem), .Dados(register_1_q),
    .\Endereço (multiplexer_1_out), .Store(controller_1_write), .Load(controller_1_read),
    .Select(controller_1_sel), .Enable_RDM(controller_1_cargardm), .\Saída (\memory_block_1_saída ));  // open: Clear
  OpCode opcode_1 (
    .CargaRI(controller_1_cargari), .Clock(clock_1_out), .Entrada(\memory_block_1_saída ),
    .\Saída (\opcode_1_saída ));  // open: Reset
  Decoder #(.select(4)) decoder_1 (
    .out0(decoder_1_out0), .out1(decoder_1_out1), .out2(decoder_1_out2), .out3(decoder_1_out3),
    .out4(decoder_1_out4), .out5(decoder_1_out5), .out6(decoder_1_out6), .out7(decoder_1_out7),
    .out8(decoder_1_out8), .out9(decoder_1_out9), .out10(decoder_1_out10), .sel(\opcode_1_saída ));  // open: out11, out12, out13, out14, out15, en
  Controller controller_1 (
    .cargaPC(controller_1_cargapc), .cargaNZ(controller_1_carganz), .cargaAC(controller_1_cargaac),
    .ulaNot(controller_1_ulanot), .ulaAnd(controller_1_ulaand), .ulaOr(controller_1_ulaor),
    .ulaAdd(controller_1_ulaadd), .write(controller_1_write), .read(controller_1_read),
    .cargaRDM(controller_1_cargardm), .sel(controller_1_sel), .cargaRI(controller_1_cargari),
    .incrementaPC(controller_1_incrementapc), .cargaREM(controller_1_cargarem), .NOP(decoder_1_out10),
    .STA(decoder_1_out9), .LDA(decoder_1_out8), .ADD(decoder_1_out7), .OR(decoder_1_out6),
    .AND(decoder_1_out5), .NOT(decoder_1_out4), .JMP(decoder_1_out3), .JN(decoder_1_out2),
    .JZ(decoder_1_out1), .HLT(decoder_1_out0), .N(ula_v2_1_n), .Z(ula_v2_1_z), .clk(clock_1_out));  // open: rst, gotot0, ulaY
endmodule

module main3 (
  input  clock,
  input  reset
);

  wire controller_1_cargaac, controller_1_carganz, controller_1_cargapc, controller_1_cargardm,
       controller_1_cargarem, controller_1_cargari, controller_1_incrementapc, controller_1_read,
       controller_1_sel, controller_1_ulaadd, controller_1_ulaand, controller_1_ulanot, controller_1_ulaor,
       controller_1_ulay, controller_1_write, decoder_1_out0, decoder_1_out1, decoder_1_out2, decoder_1_out3,
       decoder_1_out4, decoder_1_out5, decoder_1_out6, decoder_1_out8, decoder_1_out9, decoder_1_out10,
       decoder_1_out15, not_1_out, not_2_out, or_1_out, ula_v2_1_n, ula_v2_1_z;
  wire [2:0] instruction_decoder_1_out_5;
  wire [3:0] \opcode_1_saída ;
  wire [7:0] counter_1_q, \memory_block_1_saída , multiplexer_1_out, multiplexer_2_out, ula_v2_1_ac_exit,
       ula_v2_1_exit;

  ULA_v2 ula_v2_1 (
    .A(\memory_block_1_saída ), .Select(instruction_decoder_1_out_5), .Exit(ula_v2_1_exit), .Z(ula_v2_1_z),
    .N(ula_v2_1_n), .Clock(clock), .Enable(controller_1_cargaac), .Carga_NZ(controller_1_carganz),
    .AC_Exit(ula_v2_1_ac_exit));  // open: Clear
  Instruction_Decoder instruction_decoder_1 (
    .add(controller_1_ulaadd), .\and (controller_1_ulaand), .\or (controller_1_ulaor),
    .\not (controller_1_ulanot), .out_5(instruction_decoder_1_out_5));
  Multiplexer #(.width(8)) multiplexer_1 (
    .in0(ula_v2_1_exit), .in1(ula_v2_1_ac_exit), .out(multiplexer_1_out), .sel(not_1_out));  // open: en
  not not_1 (not_1_out, controller_1_ulay);
  // Probe on \memory_block_1_saída 
  Counter counter_1 (
    .load(controller_1_cargapc), .D(\memory_block_1_saída ), .count(controller_1_incrementapc),
    .Q(counter_1_q), .clk(clock), .clr(reset));  // open: carry
  // Probe on multiplexer_1_out
  Multiplexer #(.width(8)) multiplexer_2 (
    .in0(counter_1_q), .in1(\memory_block_1_saída ), .out(multiplexer_2_out), .sel(controller_1_sel));  // open: en
  not not_2 (not_2_out, controller_1_read);
  OpCode opcode_1 (
    .CargaRI(controller_1_cargari), .Clock(clock), .Entrada(\memory_block_1_saída ),
    .\Saída (\opcode_1_saída ), .Reset(reset));
  Memory_Block memory_block_1 (
    .Clock(clock), .Clear(reset), .Enable_REM(controller_1_cargarem), .Dados(multiplexer_1_out),
    .\Endereço (multiplexer_2_out), .Store(controller_1_write), .Load(controller_1_read), .Select(not_2_out),
    .Enable_RDM(or_1_out), .\Saída (\memory_block_1_saída ));
  Decoder #(.select(4)) decoder_1 (
    .out0(decoder_1_out0), .out1(decoder_1_out1), .out2(decoder_1_out2), .out3(decoder_1_out3),
    .out4(decoder_1_out4), .out5(decoder_1_out5), .out6(decoder_1_out6), .out8(decoder_1_out8),
    .out9(decoder_1_out9), .out10(decoder_1_out10), .out15(decoder_1_out15), .sel(\opcode_1_saída ));  // open: out7, out11, out12, out13, out14, en
  or or_1 (or_1_out, controller_1_read, controller_1_cargardm);
  Controller controller_1 (
    .rst(reset), .cargaPC(controller_1_cargapc), .cargaNZ(controller_1_carganz),
    .cargaAC(controller_1_cargaac), .ulaNot(controller_1_ulanot), .ulaAnd(controller_1_ulaand),
    .ulaOr(controller_1_ulaor), .ulaAdd(controller_1_ulaadd), .ulaY(controller_1_ulay),
    .write(controller_1_write), .read(controller_1_read), .cargaRDM(controller_1_cargardm),
    .sel(controller_1_sel), .cargaRI(controller_1_cargari), .incrementaPC(controller_1_incrementapc),
    .cargaREM(controller_1_cargarem), .NOP(decoder_1_out0), .STA(decoder_1_out1), .LDA(decoder_1_out2),
    .ADD(decoder_1_out3), .OR(decoder_1_out4), .AND(decoder_1_out5), .NOT(decoder_1_out6),
    .JMP(decoder_1_out8), .JN(decoder_1_out9), .JZ(decoder_1_out10), .HLT(decoder_1_out15), .N(ula_v2_1_n),
    .Z(ula_v2_1_z), .clk(clock));  // open: gotot0

  // Notes on the sheet:
  //   PC
endmodule
